# Fritzing sketch circuit_sketch (saved by Fritzing 0.9.3b)

parts:
  Part2 = Arduino Motor Shield (Rev3)
  hc-sr1 = hc-sr04
  J3 = Basic Servo
  M1 = DC Motor
  M2 = DC Motor
  VCC1 = Battery block 9V
  Part1 = Arduino Uno (Rev3) - ICSP  # not connected
  Part1_2 = Arduino Uno (Rev3)  # not connected
  Part3 = Triple Axis Accelerometer Breakout - ADXL335

nets:
  N1: Part2.D4, hc-sr1.Echo
  N2: Part2.D5_PWM, hc-sr1.Trig
  N3: Part2.B-, M2.pin_1
  N4: Part2.B+, M2.pin_2
  N5: Part2.A-, M1.pin_1
  N6: Part2.A+, M1.pin_2
  N7: Part2.VMOT, VCC1.+
  GND: Part2.GND, hc-sr1.GND, J3.gnd, VCC1.-, Part3.GND
  N8: Part2.D6_PWM, J3.pulse
  VCC: Part2.5V, hc-sr1.VCC, J3.vcc
